# Fritzing sketch Moturoa.EC (saved by Fritzing 0.9.3b)

parts:
  WeMos_D1_Mini1 = WeMos D1 Mini  # not connected
  WeMos_D1_Mini_Protoboard_Shield1 = WeMos D1 Mini Protoboard Shield
  R1 = Resistor [tolerance=±5% resistance=500 package=THT]

nets:
  N1: WeMos_D1_Mini_Protoboard_Shield1.A0, WeMos_D1_Mini_Protoboard_Shield1.X2-Y2, WeMos_D1_Mini_Protoboard_Shield1.X3-Y7, R1.Pin_0
  N2: WeMos_D1_Mini_Protoboard_Shield1.G, WeMos_D1_Mini_Protoboard_Shield1.X7-Y7, R1.Pin_1

custom parts:
  WeMos D1 Mini: The D1 mini is a mini wifi board based on ESP-8266EX.
