# Fritzing sketch Turbidity_bb (saved by Fritzing 0.9.3b)
breadboards: 1

parts:
  WeMos_D1_Mini1 = WeMos D1 Mini
  LED1 = LED - 3mm [color="White (6500K)" package="3 mm [THT]"]
  R1 = Photocell (LDR) [package=THT]
  R2 = Resistor [tolerance=±5% resistance=1k package="0402 [SMD]"]
  R3 = Resistor [tolerance=±5% resistance=220 package=THT]  # not connected

nets:
  N1: WeMos_D1_Mini1.5V, R1.pin_0
  N2: WeMos_D1_Mini1.A0, R1.pin_1, R2.Pin_0
  N3: WeMos_D1_Mini1.D1, LED1.anode
  N4: WeMos_D1_Mini1.G, LED1.cathode, R2.Pin_1

custom parts:
  WeMos D1 Mini: The D1 mini is a mini wifi board based on ESP-8266EX.
